# Fritzing sketch lcd (saved by Fritzing 0.9.2b)
breadboards: 1

parts:
  Raspberry_Pi1 = Raspberry Pi 2
  LCD1 = LCD screen
  R1 = Rotary Potentiometer (Small) [maximum_resistance=10kΩ package=THT]

nets:
  N1: Raspberry_Pi1.GPIO11, LCD1.DB7
  N2: Raspberry_Pi1.GPIO5, LCD1.DB6
  N3: Raspberry_Pi1.GPIO6, LCD1.DB5
  N4: Raspberry_Pi1.GPIO13, LCD1.DB4
  N5: Raspberry_Pi1.GPIO19, LCD1.E
  N6: Raspberry_Pi1.GPIO26, LCD1.RS
  GND: Raspberry_Pi1.GND, LCD1.VSS, LCD1.R/W, LCD1.LED-, R1.leg1
  5V: Raspberry_Pi1.5V, LCD1.VDD, LCD1.LED+, R1.leg2
  N7: LCD1.V0, R1.wiper
